// Logisim project CustomMultiplier.circ as structural Verilog: 1 circuit, main circuit CustomMultiplier
module CustomMultiplier (
  input  [7:0] SecondOperand,
  input  Clock,
  input  [7:0] FirstOperand,
  input  in_4,
  input  in_5,
  input  in_6,
  input  Reset,
  input  in_8,
  input  in_9,
  output [7:0] Result,
  output Done
);

  wire and_1_out, and_2_out, and_3_out, and_4_out, B_clk, not_1_out, not_2_out, or_1_out, or_2_out,
       shift_register_1_p2, shift_register_1_p3, shift_register_1_p11, shift_register_1_p12,
       shift_register_1_p13, shift_register_1_p14, shift_register_1_p15, shift_register_1_p16,
       shift_register_2_p5, shift_register_2_p6, shift_register_2_p17, shift_register_2_p18,
       shift_register_2_p19, shift_register_2_p20, shift_register_2_p21, shift_register_2_p22,
       shift_register_2_p23, shift_register_2_p24, shift_register_2_p25, shift_register_2_p26,
       shift_register_2_p27, t_ff_1_q, t_ff_2_q;
  wire [7:0] register_1_q, register_2_q;

  not not_1 (not_1_out, shift_register_1_p3);
  not not_2 (not_2_out, shift_register_2_p6);
  and and_1 (and_1_out, Clock, shift_register_1_p3);
  and and_2 (and_2_out, not_2_out, Clock);
  and and_3 (and_3_out, Clock, shift_register_2_p6);
  T_Flip_Flop t_ff_1 (.T(in_4), .clk(Clock), .Q(t_ff_1_q), .reset(Reset));  // open: Qn, preset
  buf and_4 (and_4_out, Clock);  // AND_Gate
  or or_1 (or_1_out, and_4_out, and_1_out);
  Register register_1 (
    .D(SecondOperand), .clk(Clock), .Q({register_1_q[7], in_8, register_1_q[5:0]}), .clr(Reset));  // open: en
  // OR_Gate or_2 has open pins: out=or_2_out
  Register register_2 (.D(FirstOperand), .clk(Clock), .Q(register_2_q), .clr(Reset));  // open: en
  T_Flip_Flop t_ff_2 (.T(in_5), .clk(t_ff_1_q), .Q(t_ff_2_q), .reset(Reset));  // open: Qn, preset
  T_Flip_Flop t_ff_3 (.T(in_6), .clk(t_ff_2_q), .Qn(B_clk), .reset(Reset));  // open: Q, preset
  // Shift_Register shift_register_1: pin names not known; wires that end beside it: Reset, shift_register_1_p2, shift_register_1_p3, or_1_out, in_8, register_1_q[7], in_8, register_1_q[5], register_1_q[4], register_1_q[3], shift_register_1_p11, shift_register_1_p12, shift_register_1_p13, shift_register_1_p14, shift_register_1_p15, shift_register_1_p16
  not not_3 (shift_register_1_p2, shift_register_1_p3);
  // Shift_Register shift_register_2: pin names not known; wires that end beside it: register_1_q[2], register_1_q[1], register_1_q[0], Reset, shift_register_2_p5, shift_register_2_p6, or_2_out, in_9, register_2_q[7], register_2_q[6], register_2_q[5], register_2_q[4], register_2_q[3], register_2_q[2], register_2_q[1], register_2_q[0], shift_register_2_p17, shift_register_2_p18, shift_register_2_p19, shift_register_2_p20, shift_register_2_p21, shift_register_2_p22, shift_register_2_p23, shift_register_2_p24, shift_register_2_p25, shift_register_2_p26, shift_register_2_p27
  not not_4 (shift_register_2_p5, shift_register_2_p6);
  or or_3 (shift_register_1_p3, shift_register_1_p12, shift_register_1_p13, shift_register_1_p14, shift_register_1_p15, shift_register_1_p16, shift_register_2_p17, shift_register_2_p18, shift_register_2_p19);
  or or_4 (shift_register_2_p6, shift_register_2_p20, shift_register_2_p21, shift_register_2_p22, shift_register_2_p23, shift_register_2_p24, shift_register_2_p25, shift_register_2_p26, shift_register_2_p27);

  // Other names for the same wires on the sheet: A[7:0] = FirstOperand; B[7:0] = SecondOperand; C[7:0] = Result;
  //   A_clk = Clock; clk = Clock
endmodule
